# Fritzing sketch Miernik natężenia światła i temperatury (saved by Fritzing 0.9.1b)
breadboards: 1

parts:
  LCD1 = LCD screen
  Part1 = Arduino Leonardo (Rev3b)
  R1 = Photocell (LDR) [package=THT]
  R2 = Rotary Potentiometer (Large) [maximum_resistance=10kΩ package=THT]
  R3 = Resistor [tolerance=±5% resistance=10k package="1206 [SMD]"]
  T1 = LM34 Temperature Sensor [package="TO92 [THT]"]  # not connected
  R4 = Resistor [tolerance=±5% resistance=4.7k package=THT]

nets:
  VSS: LCD1.VSS, LCD1.R/W, LCD1.LED-, Part1.GND, R2.leg1, R3.Pin_1
  VDD: LCD1.VDD, LCD1.LED+, Part1.5V, R1.pin_0, R2.leg2, R4.Pin_1
  N1: LCD1.V0, R2.wiper
  N2: LCD1.RS, Part1.D12/A11
  N3: LCD1.E, Part1.D11_PWM
  N4: LCD1.DB4, Part1.D5_PWM
  N5: LCD1.DB5, Part1.D4/A6
  N6: LCD1.DB6, Part1.D3_PWM/SCL
  N7: LCD1.DB7, Part1.D2/SDA
  N8: Part1.D7, R4.Pin_0
  N9: Part1.A0, R1.pin_1, R3.Pin_0
